// Digital circuit CPU.dig as structural Verilog
module CPU (
  input  I0,
  input  I1,
  input  I2,
  input  I3,
  input  I4,
  input  I5,
  input  I6,
  input  I7,
  input  Clr,
  input  Clk,
  output [7:0] out_11,
  output out_12,
  output out_13,
  output out_14
);

  wire Cp, Ea, instruction_register_1_c0, memory_address_register_1_s0, memory_address_register_1_s1,
       memory_address_register_1_s2, register_b_1_s0, register_b_1_s1, register_b_1_s2, register_b_1_s3,
       register_b_1_s4, register_b_1_s5, register_b_1_s6, register_b_1_s7;

  RAM ram_1 (
    .I0(I0), .I1(I1), .I2(I2), .I3(I3), .I4(I4), .I5(I5), .I6(I6), .I7(I7), .NCE(Cp), .Clr(Clr), .Clk(Clk),
    .A(memory_address_register_1_s0), .B(memory_address_register_1_s1), .C(memory_address_register_1_s2),
    .S0(I0), .S1(I1), .S2(I2), .S3(I3), .S4(I4), .S5(I5), .S6(I6), .S7(I7));
  Instruction_Register instruction_register_1 (
    .NEi(Cp), .Clr(Clr), .Clk(Clk), .NLi(Cp), .I0(I0), .I1(I1), .I2(I2), .I3(I3), .I4(I4), .I5(I5), .I6(I6),
    .I7(I7), .C0(instruction_register_1_c0), .C1(instruction_register_1_c0), .C2(instruction_register_1_c0),
    .C3(instruction_register_1_c0), .Op0(I4), .Op1(I5), .Op2(I6), .Op3(I7));
  Ring_Counter ring_counter_1 (.Clk(Clk), .Clr(Clr), .Q3(Cp), .Q4(Cp), .Q5(Cp));  // open: Q0, Q1, Q2
  Program_Counter program_counter_1 (
    .Cp(Cp), .Ep(Cp), .NClr(Clr), .NClk(Clk), .S0(I0), .S1(I1), .S2(I2), .S3(I3), .S4(I4), .S5(I5), .S6(I6),
    .S7(I7));
  Memory_Address_Register memory_address_register_1 (
    .NLm(Cp), .Clk(Clk), .I0(I0), .I1(I1), .I2(I2), .S0(memory_address_register_1_s0),
    .S1(memory_address_register_1_s1), .S2(memory_address_register_1_s2));  // open: I3, S3, S4, S5, S6, S7
  Register_B register_b_1 (
    .NLb(Cp), .Clk(Clk), .I0(I0), .I1(I1), .I2(I2), .I3(I3), .I4(I4), .I5(I5), .I6(I6), .I7(I7),
    .S0(register_b_1_s0), .S1(register_b_1_s1), .S2(register_b_1_s2), .S3(register_b_1_s3),
    .S4(register_b_1_s4), .S5(register_b_1_s5), .S6(register_b_1_s6), .S7(register_b_1_s7));
  Register_OUT register_out_1 (
    .NLo(Cp), .Clk(Clk), .I0(I0), .I1(I1), .I2(I2), .I3(I3), .I4(I4), .I5(I5), .I6(I6), .I7(I7),
    .S0(out_11[0]), .S1(out_11[1]), .S2(out_11[2]), .S3(out_11[3]), .S4(out_11[4]), .S5(out_11[5]),
    .S6(out_11[6]), .S7(out_11[7]));
  Acumulator acumulator_1 (
    .NLa(Cp), .Ea(Ea), .Clk(Clk), .I0(I0), .I1(I1), .I2(I2), .I3(I3), .I4(I4), .I5(I5), .I6(I6), .I7(I7),
    .S0(I0), .S1(I1), .S2(I2), .S3(I3), .S4(I4), .S5(I5), .S6(I6), .S7(I7));
  ULA ula_1 (
    .A0(I0), .B0(register_b_1_s0), .A1(I1), .B1(register_b_1_s1), .A2(I2), .B2(register_b_1_s2), .A3(I3),
    .B3(register_b_1_s3), .A4(I4), .B4(register_b_1_s4), .A5(I5), .B5(register_b_1_s5), .A6(I6),
    .B6(register_b_1_s6), .A7(I7), .B7(register_b_1_s7), .out_20(out_12), .eq(out_13), .plus(out_14),
    .S0(I0), .S1(I1), .S2(I2), .S3(I3), .S4(I4), .S5(I5), .S6(I6), .S7(I7));  // open: C0, C1, C2, Eu
  // Pins of 1 and 8 bits meet at out_11
  // also tied to GND on the sheet: instruction_register_1_c0

  // Other names for the same wires on the sheet: Ep = Cp; NCE = Cp; NEi = Cp; NLa = Cp; NLb = Cp; NLi = Cp; NLm = Cp;
  //   NLo = Cp
endmodule
